# Fritzing sketch HomePlantProject (saved by Fritzing 0.9.9b)

parts:
  GY-1 = GY-302 [part_number=GY-302]
  KY-1 = Keyes Relay [package=THT]
  LLC1 = Logic Level Converter [package="Breakout board"]
  U3 = NodeMCU V1.0
  R6 = Resistor [tolerance=±5% resistance=10k package="0402 [SMD]"]
  Part1 = Adafruit AHT20 Temperature and Humidity Sensor [part_number="Adafruit #4566"]  # not connected
  S1 = Pushbutton [package="[THT]"]

nets:
  N1: GY-1.SDA, U3.D2
  N2: GY-1.SCL, U3.D1
  N3: GY-1.GND, U3.GND#6
  N4: GY-1.VCC, U3.3V3#5
  N5: KY-1.signal, LLC1.HV3
  N6: LLC1.LV, U3.3V3#19
  N7: LLC1.LV3, U3.D7
  N8: U3.D6, U3.3V3#14, R6.Pin_0, S1.Pin_3, S1.Pin_4
  N9: U3.GND#13, R6.Pin_1

notes:
  Home Plant Project
  BH1750
  Esp8266 (Nodemcu )
  Logic Level Converter
  5v Relay
  10 kΩ
  AHT10
  EEPROM RESET

custom parts:
  Keyes Relay: The Keyes 5V relay module is suitable for SCM development, home appliance control. It uses a 5V~12V TIL control signal which can control DC / AC signal.
  Logic Level Converter: 5V to/from 3.3V logic level converter
  NodeMCU V1.0: ESP8266 based NodeMCU V1.0
  Adafruit AHT20 Temperature and Humidity Sensor: The AHT20 is a nice but inexpensive temperature and humidity sensor from the same folks that brought us the DHT22. You can take sensor readings as often as you like, and it uses standard I2C so its super easy to use with any Arduino or Linux/Raspberry Pi board. This sensor has a typical accuracy of +- 2% relative humidity, and +-0.3 °C. There is only one I2C address so its not a good option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

// code stored in the sketch: Untitled.ino

